# Fritzing sketch Breadboard LED Strip v1 (saved by Fritzing 0.8.0b)
breadboards: 1

parts:
  R1 = Resistor [tolerance=±5% resistance=220 package="0603 [SMD]"]
  R2 = Resistor [tolerance=±5% resistance=220 package="0603 [SMD]"]
  R3 = Resistor [tolerance=±5% resistance=220 package="0603 [SMD]"]
  R4 = Resistor [tolerance=±5% resistance=220 package="0603 [SMD]"]
  R5 = Resistor [tolerance=±5% resistance=220 package="0603 [SMD]"]
  R6 = Resistor [tolerance=±5% resistance=220 package="0603 [SMD]"]
  R7 = Resistor [tolerance=±5% resistance=220 package="0603 [SMD]"]
  R8 = Resistor [tolerance=±5% resistance=220 package="0603 [SMD]"]
  R9 = Resistor [tolerance=±5% resistance=220 package="0603 [SMD]"]
  R10 = Resistor [tolerance=±5% resistance=220 package="0603 [SMD]"]
  LED1 = smd LED [color="Red (633nm)" package="0603 [SMD]"]
  LED2 = smd LED [color="Red (633nm)" package="0603 [SMD]"]
  LED3 = smd LED [color="Red (633nm)" package="0603 [SMD]"]
  LED4 = smd LED [color="Red (633nm)" package="0603 [SMD]"]
  LED5 = smd LED [color="Red (633nm)" package="0603 [SMD]"]
  LED6 = smd LED [color="Red (633nm)" package="0603 [SMD]"]
  LED7 = smd LED [color="Red (633nm)" package="0603 [SMD]"]
  LED8 = smd LED [color="Red (633nm)" package="0603 [SMD]"]
  LED9 = smd LED [color="Red (633nm)" package="0603 [SMD]"]
  LED10 = smd LED [color="Red (633nm)" package="0603 [SMD]"]
  Common = female pin header, 11 pins [form="♀ (female)"]
  Common_2 = female pin header, 11 pins [form="♀ (female)"]
  R11 = Resistor [tolerance=±5% resistance=220 package="0603 [SMD]"]
  R12 = Resistor [tolerance=±5% resistance=220 package="0603 [SMD]"]
  R13 = Resistor [tolerance=±5% resistance=220 package="0603 [SMD]"]
  R14 = Resistor [tolerance=±5% resistance=220 package="0603 [SMD]"]
  R15 = Resistor [tolerance=±5% resistance=220 package="0603 [SMD]"]
  R16 = Resistor [tolerance=±5% resistance=220 package="0603 [SMD]"]
  R17 = Resistor [tolerance=±5% resistance=220 package="0603 [SMD]"]
  R18 = Resistor [tolerance=±5% resistance=220 package="0603 [SMD]"]
  R19 = Resistor [tolerance=±5% resistance=220 package="0603 [SMD]"]
  R20 = Resistor [tolerance=±5% resistance=220 package="0603 [SMD]"]
  LED11 = smd LED [color="Red (633nm)" package="0603 [SMD]"]
  LED12 = smd LED [color="Red (633nm)" package="0603 [SMD]"]
  LED13 = smd LED [color="Red (633nm)" package="0603 [SMD]"]
  LED14 = smd LED [color="Red (633nm)" package="0603 [SMD]"]
  LED15 = smd LED [color="Red (633nm)" package="0603 [SMD]"]
  LED16 = smd LED [color="Red (633nm)" package="0603 [SMD]"]
  LED17 = smd LED [color="Red (633nm)" package="0603 [SMD]"]
  LED18 = smd LED [color="Red (633nm)" package="0603 [SMD]"]
  LED19 = smd LED [color="Red (633nm)" package="0603 [SMD]"]
  LED20 = smd LED [color="Red (633nm)" package="0603 [SMD]"]
  Common_3 = female pin header, 11 pins [form="♀ (female)"]
  R21 = Resistor [tolerance=±5% resistance=220 package="0603 [SMD]"]
  R22 = Resistor [tolerance=±5% resistance=220 package="0603 [SMD]"]
  R23 = Resistor [tolerance=±5% resistance=220 package="0603 [SMD]"]
  R24 = Resistor [tolerance=±5% resistance=220 package="0603 [SMD]"]
  R25 = Resistor [tolerance=±5% resistance=220 package="0603 [SMD]"]
  R26 = Resistor [tolerance=±5% resistance=220 package="0603 [SMD]"]
  R27 = Resistor [tolerance=±5% resistance=220 package="0603 [SMD]"]
  R28 = Resistor [tolerance=±5% resistance=220 package="0603 [SMD]"]
  R29 = Resistor [tolerance=±5% resistance=220 package="0603 [SMD]"]
  R30 = Resistor [tolerance=±5% resistance=220 package="0603 [SMD]"]
  LED21 = smd LED [color="Red (633nm)" package="0603 [SMD]"]
  LED22 = smd LED [color="Red (633nm)" package="0603 [SMD]"]
  LED23 = smd LED [color="Red (633nm)" package="0603 [SMD]"]
  LED24 = smd LED [color="Red (633nm)" package="0603 [SMD]"]
  LED25 = smd LED [color="Red (633nm)" package="0603 [SMD]"]
  LED26 = smd LED [color="Red (633nm)" package="0603 [SMD]"]
  LED27 = smd LED [color="Red (633nm)" package="0603 [SMD]"]
  LED28 = smd LED [color="Red (633nm)" package="0603 [SMD]"]
  LED29 = smd LED [color="Red (633nm)" package="0603 [SMD]"]
  LED30 = smd LED [color="Red (633nm)" package="0603 [SMD]"]
  Common_4 = female pin header, 11 pins [form="♀ (female)"]
  R31 = Resistor [tolerance=±5% resistance=220 package="0603 [SMD]"]
  R32 = Resistor [tolerance=±5% resistance=220 package="0603 [SMD]"]
  R33 = Resistor [tolerance=±5% resistance=220 package="0603 [SMD]"]
  R34 = Resistor [tolerance=±5% resistance=220 package="0603 [SMD]"]
  R35 = Resistor [tolerance=±5% resistance=220 package="0603 [SMD]"]
  R36 = Resistor [tolerance=±5% resistance=220 package="0603 [SMD]"]
  R37 = Resistor [tolerance=±5% resistance=220 package="0603 [SMD]"]
  R38 = Resistor [tolerance=±5% resistance=220 package="0603 [SMD]"]
  R39 = Resistor [tolerance=±5% resistance=220 package="0603 [SMD]"]
  R40 = Resistor [tolerance=±5% resistance=220 package="0603 [SMD]"]
  LED31 = smd LED [color="Red (633nm)" package="0603 [SMD]"]
  LED32 = smd LED [color="Red (633nm)" package="0603 [SMD]"]
  LED33 = smd LED [color="Red (633nm)" package="0603 [SMD]"]
  LED34 = smd LED [color="Red (633nm)" package="0603 [SMD]"]
  LED35 = smd LED [color="Red (633nm)" package="0603 [SMD]"]
  LED36 = smd LED [color="Red (633nm)" package="0603 [SMD]"]
  LED37 = smd LED [color="Red (633nm)" package="0603 [SMD]"]
  LED38 = smd LED [color="Red (633nm)" package="0603 [SMD]"]
  LED39 = smd LED [color="Red (633nm)" package="0603 [SMD]"]
  LED40 = smd LED [color="Red (633nm)" package="0603 [SMD]"]

nets:
  N1: R1.Pin_0, LED1.anode
  N2: R1.Pin_1, Common.pin10
  N3: R2.Pin_0, LED2.anode
  N4: R2.Pin_1, Common.pin9
  N5: R3.Pin_0, LED3.anode
  N6: R3.Pin_1, Common.pin8
  N7: R4.Pin_0, LED4.anode
  N8: R4.Pin_1, Common.pin7
  N9: R5.Pin_0, LED5.anode
  N10: R5.Pin_1, Common.pin6
  N11: R6.Pin_0, LED6.anode
  N12: R6.Pin_1, Common.pin5
  N13: R7.Pin_0, LED7.anode
  N14: R7.Pin_1, Common.pin4
  N15: R8.Pin_0, LED8.anode
  N16: R8.Pin_1, Common.pin3
  N17: R9.Pin_0, LED9.anode
  N18: R9.Pin_1, Common.pin2
  N19: R10.Pin_0, LED10.anode
  N20: R10.Pin_1, Common.pin1
  N21: LED1.cathode, LED2.cathode, LED3.cathode, LED4.cathode, LED5.cathode, LED6.cathode, LED7.cathode, LED8.cathode, LED9.cathode, LED10.cathode, Common.pin11
  N22: Common_2.pin1, R11.Pin_1
  N23: Common_2.pin2, R12.Pin_1
  N24: Common_2.pin3, R13.Pin_1
  N25: Common_2.pin4, R14.Pin_1
  N26: Common_2.pin5, R15.Pin_1
  N27: Common_2.pin6, R16.Pin_1
  N28: Common_2.pin7, R17.Pin_1
  N29: Common_2.pin8, R18.Pin_1
  N30: Common_2.pin9, R19.Pin_1
  N31: Common_2.pin10, R20.Pin_1
  N32: Common_2.pin11, LED11.cathode, LED12.cathode, LED13.cathode, LED14.cathode, LED15.cathode, LED16.cathode, LED17.cathode, LED18.cathode, LED19.cathode, LED20.cathode
  N33: R11.Pin_0, LED11.anode
  N34: R12.Pin_0, LED12.anode
  N35: R13.Pin_0, LED13.anode
  N36: R14.Pin_0, LED14.anode
  N37: R15.Pin_0, LED15.anode
  N38: R16.Pin_0, LED16.anode
  N39: R17.Pin_0, LED17.anode
  N40: R18.Pin_0, LED18.anode
  N41: R19.Pin_0, LED19.anode
  N42: R20.Pin_0, LED20.anode
  N43: Common_3.pin1, R21.Pin_1
  N44: Common_3.pin2, R22.Pin_1
  N45: Common_3.pin3, R23.Pin_1
  N46: Common_3.pin4, R24.Pin_1
  N47: Common_3.pin5, R25.Pin_1
  N48: Common_3.pin6, R26.Pin_1
  N49: Common_3.pin7, R27.Pin_1
  N50: Common_3.pin8, R28.Pin_1
  N51: Common_3.pin9, R29.Pin_1
  N52: Common_3.pin10, R30.Pin_1
  N53: Common_3.pin11, LED21.cathode, LED22.cathode, LED23.cathode, LED24.cathode, LED25.cathode, LED26.cathode, LED27.cathode, LED28.cathode, LED29.cathode, LED30.cathode
  N54: R21.Pin_0, LED21.anode
  N55: R22.Pin_0, LED22.anode
  N56: R23.Pin_0, LED23.anode
  N57: R24.Pin_0, LED24.anode
  N58: R25.Pin_0, LED25.anode
  N59: R26.Pin_0, LED26.anode
  N60: R27.Pin_0, LED27.anode
  N61: R28.Pin_0, LED28.anode
  N62: R29.Pin_0, LED29.anode
  N63: R30.Pin_0, LED30.anode
  N64: Common_4.pin1, R31.Pin_1
  N65: Common_4.pin2, R32.Pin_1
  N66: Common_4.pin3, R33.Pin_1
  N67: Common_4.pin4, R34.Pin_1
  N68: Common_4.pin5, R35.Pin_1
  N69: Common_4.pin6, R36.Pin_1
  N70: Common_4.pin7, R37.Pin_1
  N71: Common_4.pin8, R38.Pin_1
  N72: Common_4.pin9, R39.Pin_1
  N73: Common_4.pin10, R40.Pin_1
  N74: Common_4.pin11, LED31.cathode, LED32.cathode, LED33.cathode, LED34.cathode, LED35.cathode, LED36.cathode, LED37.cathode, LED38.cathode, LED39.cathode, LED40.cathode
  N75: R31.Pin_0, LED31.anode
  N76: R32.Pin_0, LED32.anode
  N77: R33.Pin_0, LED33.anode
  N78: R34.Pin_0, LED34.anode
  N79: R35.Pin_0, LED35.anode
  N80: R36.Pin_0, LED36.anode
  N81: R37.Pin_0, LED37.anode
  N82: R38.Pin_0, LED38.anode
  N83: R39.Pin_0, LED39.anode
  N84: R40.Pin_0, LED40.anode

notes:
  ------------------------------------
